# Fritzing sketch stm32 (saved by Fritzing 0.9.3b)
breadboards: 1

parts:
  M1 = STM32F103C8T6 blue mini board
  R1 = Photocell (LDR) [package=THT]
  R2 = Photocell (LDR) [package=THT]
  Grove1 = Grove OLED 128x96
  R3 = Resistor [tolerance=±1% resistance=4.7k package=THT]
  R4 = Resistor [tolerance=±1% resistance=4.7k package=THT]

nets:
  N1: M1.B6, Grove1.SCL
  N2: M1.B7, M1.B8, Grove1.SDA
  N3: M1.C15, M1.A0, R1.pin_1, R3.Pin_0
  N4: M1.A1, R2.pin_1, R4.Pin_0
  3.3V: M1.3.3V, Grove1.VCC, R3.Pin_1, R4.Pin_1
  GND: M1.G, M1.GND, R1.pin_0, R2.pin_0, Grove1.GND
